// Logisim project alu.circ as structural Verilog: 1 circuit, main circuit alu
module alu (
  input  [31:0] A,
  input  [31:0] B,
  input  [3:0] ALUSel,
  output [31:0] Result
);

  wire multiplexer_2_out;
  wire [31:0] add_slt_sub, adder_1_out, and1, bit_extender_1_out, mul10, mulh14, mulhu11, multiplexer_1_out,
       not_1_out, or2, sll6, sra5, srl4, xor3;

  Multiplexer #(.enable("false"), .width(32)) multiplexer_1 (
    .in0(B), .in1(not_1_out), .out(multiplexer_1_out), .sel(ALUSel[2]));
  assign not_1_out = ~B;  // NOT_Gate not_1, 32 bits wide
  assign and1 = A & B;  // AND_Gate and_1, 32 bits wide
  assign or2 = A | B;  // OR_Gate or_1, 32 bits wide
  assign xor3 = A ^ B;  // XOR_Gate xor_1, 32 bits wide
  Shifter #(.shift("lr"), .width(32)) shifter_1 (.in(A), .\dist (B[4:0]), .out(srl4));
  Shifter #(.shift("ar"), .width(32)) shifter_2 (.in(A), .\dist (B[4:0]), .out(sra5));
  Shifter #(.width(32)) shifter_3 (.in(A), .\dist (B[4:0]), .out(sll6));
  Multiplier #(.mode("twosComplement"), .width(32)) multiplier_1 (
    .a(A), .b(B), .out(mul10), .cout(mulh14));  // open: cin
  Multiplier #(.width(32)) multiplier_2 (.a(A), .b(B), .cout(mulhu11));  // open: out, cin
  Multiplexer #(.enable("false")) multiplexer_2 (.in0(1'b0), .in1(1'b1), .out(multiplexer_2_out), .sel(ALUSel[2]));
  Adder #(.width(32)) adder_1 (.a(A), .b(multiplexer_1_out), .out(adder_1_out), .cin(multiplexer_2_out));  // open: cout
  Multiplexer #(.enable("false"), .width(32)) multiplexer_3 (
    .in0(adder_1_out), .in1(bit_extender_1_out), .out(add_slt_sub), .sel(ALUSel[0]));
  assign bit_extender_1_out = {{31{1'b0}}, adder_1_out[31]};  // Bit_Extender bit_extender_1
  Multiplexer #(.enable("false"), .select(4), .width(32)) multiplexer_4 (
    .in0(add_slt_sub), .in1(and1), .in2(or2), .in3(xor3), .in4(srl4), .in5(sra5), .in6(sll6),
    .in7(add_slt_sub), .in10(mul10), .in11(mulhu11), .in12(add_slt_sub), .in13(B), .in14(mulh14),
    .out(Result), .sel(ALUSel));  // open: in8, in9, in15

  // Other names for the same wires on the sheet: SLT = ALUSel[0]; B_INVERT = ALUSel[2]; B_LOW_5[4:0] = B[4:0]

  // Notes on the sheet:
  //   INPUTS to your circuit
  //   DON'T CHANGE THE LOCATIONS OF THE INPUTS AND OUTPUTS!
  //   OUTPUT from your circuit
endmodule
