// Logisim project branch_comp.circ as structural Verilog: 1 circuit, main circuit branch_comp
module branch_comp (
  input  [31:0] rs1,
  input  [31:0] rs2,
  input  BrUn,
  output BrEq,
  output BrLt
);

  wire SignedBrEq, SignedBrLt, UnsignedBrEq, UnsignedBrLt;

  Comparator #(.width(32)) comparator_1 (.a(rs1), .b(rs2), .eq(SignedBrEq), .lt(SignedBrLt));  // open: gt
  Comparator #(.mode("unsigned"), .width(32)) comparator_2 (
    .a(rs1), .b(rs2), .eq(UnsignedBrEq), .lt(UnsignedBrLt));  // open: gt
  Multiplexer #(.enable("false")) multiplexer_1 (.in0(SignedBrEq), .in1(UnsignedBrEq), .out(BrEq), .sel(BrUn));
  Multiplexer #(.enable("false")) multiplexer_2 (.in0(SignedBrLt), .in1(UnsignedBrLt), .out(BrLt), .sel(BrUn));

  // Notes on the sheet:
  //   INPUTS to your circuit
  //   DON'T CHANGE THE LOCATIONS OF THE INPUTS AND OUTPUTS!
  //   OUTPUT from your circuit
endmodule
