// Logisim project control_logic.circ as structural Verilog: 1 circuit, main circuit control_logic
module control_logic (
  input  [31:0] inst,
  input  BrEq,
  input  BrLt,
  output PCSel,
  output RegWEn,
  output [2:0] ImmSel,
  output BrUn,
  output ASel,
  output BSel,
  output [3:0] ALUSel,
  output MemRW,
  output [1:0] WBSel,
  output CSRSel,
  output CSRWen,
  output [1:0] MemRWNumBytes
);

  wire ALU_add, ALU_and, ALU_B, ALU_mul, ALU_mulh, ALU_mulhu, ALU_or, ALU_sll, ALU_slt, ALU_sra, ALU_srl,
       ALU_xor, Arithmetic, beq_taken, bge_bgeu_taken, blt_bltu_taken, bnq_taken, I_Type, I_Type_Arithmetic,
       I_Type_jalr, I_Type_Load, R_Type, SB_Type, sub, U_Type, U_Type_auipc, UJ_Type_jal, WB_ALU,
       WB_PC_Plus_4;

  and and_1 (R_Type, ~inst[2], ~inst[3], inst[4], inst[5], ~inst[6]);  // AND_Gate
  and and_2 (I_Type_Load, ~inst[2], ~inst[3], ~inst[4], ~inst[5], ~inst[6]);  // AND_Gate
  and and_3 (I_Type_Arithmetic, ~inst[2], ~inst[3], inst[4], ~inst[5], ~inst[6]);  // AND_Gate
  and and_4 (MemRW, ~inst[2], ~inst[3], ~inst[4], inst[5], ~inst[6]);  // AND_Gate
  and and_5 (SB_Type, ~inst[2], ~inst[3], ~inst[4], inst[5], inst[6]);  // AND_Gate
  or or_1 (Arithmetic, I_Type_Arithmetic, R_Type);
  and and_6 (ALU_and, Arithmetic, inst[12], inst[13], inst[14]);
  and and_7 (ALU_or, Arithmetic, ~inst[12], inst[13], inst[14]);  // AND_Gate
  and and_8 (ALU_xor, Arithmetic, ~inst[12], ~inst[13], inst[14]);  // AND_Gate
  and and_9 (ALU_srl, Arithmetic, inst[12], ~inst[13], inst[14], ~inst[30]);  // AND_Gate
  and and_10 (ALU_sra, Arithmetic, inst[12], ~inst[13], inst[14], inst[30]);  // AND_Gate
  and and_11 (U_Type_auipc, inst[2], ~inst[3], inst[4], ~inst[5], ~inst[6]);  // AND_Gate
  and and_12 (ALU_B, inst[2], ~inst[3], inst[4], inst[5], ~inst[6]);  // AND_Gate
  and and_13 (UJ_Type_jal, inst[2], inst[3], ~inst[4], inst[5], inst[6]);  // AND_Gate
  and and_14 (I_Type_jalr, inst[2], ~inst[3], ~inst[4], inst[5], inst[6]);  // AND_Gate
  and and_15 (CSRWen, ~inst[2], ~inst[3], inst[4], inst[5], inst[6]);  // AND_Gate
  and and_16 (ALU_sll, Arithmetic, inst[12], ~inst[13], ~inst[14], ~inst[25]);  // AND_Gate
  and and_17 (ALU_slt, Arithmetic, ~inst[12], inst[13], ~inst[14]);  // AND_Gate
  and and_18 (ALU_mul, R_Type, ~inst[12], ~inst[13], ~inst[14], inst[25]);  // AND_Gate
  and and_19 (ALU_mulhu, R_Type, inst[12], inst[13], ~inst[14]);  // AND_Gate
  and and_20 (sub, R_Type, ~inst[12], ~inst[13], ~inst[14], inst[30]);  // AND_Gate
  and and_21 (ALU_mulh, R_Type, inst[12], ~inst[13], ~inst[14], inst[25]);  // AND_Gate
  and and_22 (beq_taken, SB_Type, ~inst[12], ~inst[13], ~inst[14], BrEq);  // AND_Gate
  and and_23 (bnq_taken, SB_Type, inst[12], ~inst[13], ~inst[14], ~BrEq);  // AND_Gate
  and and_24 (blt_bltu_taken, SB_Type, ~inst[12], inst[14], BrLt);  // AND_Gate
  and and_25 (bge_bgeu_taken, SB_Type, inst[12], inst[14], ~BrLt);  // AND_Gate
  nor nor_1 (ALU_add, ALU_and, ALU_or, ALU_xor, ALU_srl, ALU_sra, ALU_sll, ALU_slt, ALU_mul, ALU_mulhu, ALU_B, sub, ALU_mulh);
  or or_2 (PCSel, beq_taken, bnq_taken, blt_bltu_taken, bge_bgeu_taken, UJ_Type_jal, I_Type_jalr);
  nor nor_2 (RegWEn, MemRW, SB_Type);
  and and_26 (BrUn, inst[13], SB_Type);
  Priority_Encoder #(.select(4)) priority_encoder_1 (
    .in0(ALU_add), .in1(ALU_and), .in2(ALU_or), .in3(ALU_xor), .in4(ALU_srl), .in5(ALU_sra), .in6(ALU_sll),
    .in7(ALU_slt), .in10(ALU_mul), .in11(ALU_mulhu), .in12(sub), .in13(ALU_B), .in14(ALU_mulh), .out(ALUSel));  // open: in8, in9, in15, gs, en_out, en_in
  or or_3 (I_Type, I_Type_Arithmetic, I_Type_Load, I_Type_jalr, CSRWen);
  or or_4 (U_Type, U_Type_auipc, ALU_B);
  Priority_Encoder priority_encoder_2 (
    .in0(I_Type), .in1(MemRW), .in2(SB_Type), .in3(U_Type), .in4(UJ_Type_jal), .out(ImmSel));  // open: in5, in6, in7, en_in, gs, en_out
  not not_1 (BSel, R_Type);
  or or_5 (ASel, SB_Type, UJ_Type_jal, U_Type_auipc);
  or or_6 (WB_PC_Plus_4, UJ_Type_jal, I_Type_jalr);
  Priority_Encoder #(.select(2)) priority_encoder_3 (
    .in0(WB_ALU), .in1(I_Type_Load), .in2(WB_PC_Plus_4), .out(WBSel));  // open: in3, gs, en_out, en_in
  or or_7 (WB_ALU, R_Type, I_Type_Arithmetic, U_Type_auipc, ALU_B);
  and and_27 (CSRSel, CSRWen, inst[14]);

  assign MemRWNumBytes = inst[13:12];

  // Other names for the same wires on the sheet: I_Type_csrw = CSRWen; I_2 = inst[2]; I_3 = inst[3]; I_4 = inst[4];
  //   I_5 = inst[5]; I_6 = inst[6]; I_14 = inst[14]; I_25 = inst[25]; I_30 = inst[30]; I_12 = inst[12];
  //   I_13 = inst[13]; S_Type = MemRW; U_Type_lui = ALU_B

  // Notes on the sheet:
  //   INPUTS to your circuit
  //   Select identification bits
  //   DON'T CHANGE THE LOCATIONS OF THE INPUTS AND OUTPUTS!
  //   OUTPUT from your circuit
  //   Decode Instruction Types
  //   PCSel
  //   ImmSel
  //   BrUn
  //   RegWEn
endmodule
