// Logisim project imm_gen.circ as structural Verilog: 1 circuit, main circuit imm_gen
module imm_gen (
  input  [31:0] inst,
  input  [2:0] ImmSel,
  output [31:0] imm
);

  wire [31:0] I_IMM, S_IMM, SB_IMM, UJ_IMM;

  assign I_IMM = {{20{inst[31]}}, inst[31:20]};  // Bit_Extender bit_extender_1
  assign S_IMM = {{20{inst[31]}}, {inst[31:25], inst[11:7]}};  // Bit_Extender bit_extender_2
  assign SB_IMM = {{19{inst[31]}}, {inst[31], inst[7], inst[30:25], inst[11:8], 1'b0}};  // Bit_Extender bit_extender_3
  assign UJ_IMM = {{11{inst[31]}}, {inst[31], inst[19:12], inst[20], inst[30:21], 1'b0}};  // Bit_Extender bit_extender_4
  Multiplexer #(.enable("false"), .select(3), .width(32)) multiplexer_1 (
    .in0(I_IMM), .in1(S_IMM), .in2(SB_IMM), .in3({inst[31:12], {12{1'b0}}}), .in4(UJ_IMM), .out(imm),
    .sel(ImmSel));  // open: in5, in6, in7

  // Other names for the same wires on the sheet: I_8_11[3:0] = inst[11:8]; I_7 = inst[7]; I_21_24[3:0] = inst[24:21];
  //   U_IMM[31:12] = inst[31:12]; I_25_30[5:0] = inst[30:25]; I_20 = inst[20]; I_12_19[7:0] = inst[19:12];
  //   I_31 = inst[31]

  // Notes on the sheet:
  //   INPUTS to your circuit
  //   DON'T CHANGE THE LOCATIONS OF THE INPUTS AND OUTPUTS!
  //   OUTPUT from your circuit
endmodule
