// Logisim project regfile.circ as structural Verilog: 1 circuit, main circuit regfile
module regfile (
  input  [4:0] rs1,
  input  [4:0] rs2,
  input  [4:0] rd,
  input  [31:0] Write_Data,
  input  RegWEn,
  input  clk,
  output [31:0] ra,
  output [31:0] sp,
  output [31:0] t0,
  output [31:0] t1,
  output [31:0] t2,
  output [31:0] s0,
  output [31:0] s1,
  output [31:0] a0,
  output [31:0] Read_Data_1,
  output [31:0] Read_Data_2
);

  wire decoder_1_out0, decoder_1_out1, decoder_1_out2, decoder_1_out3, decoder_1_out4, decoder_1_out5,
       decoder_1_out6, decoder_1_out7, decoder_1_out8, decoder_1_out9, decoder_1_out10, decoder_1_out11,
       decoder_1_out12, decoder_1_out13, decoder_1_out14, decoder_1_out15, decoder_1_out16, decoder_1_out17,
       decoder_1_out18, decoder_1_out19, decoder_1_out20, decoder_1_out21, decoder_1_out22, decoder_1_out23,
       decoder_1_out24, decoder_1_out25, decoder_1_out26, decoder_1_out27, decoder_1_out28, decoder_1_out29,
       decoder_1_out30, decoder_1_out31, WE0, WE1, WE2, WE3, WE4, WE5, WE6, WE7, WE8, WE9, WE10, WE11, WE12,
       WE13, WE14, WE15, WE16, WE17, WE18, WE19, WE20, WE21, WE22, WE23, WE24, WE25, WE26, WE27, WE28, WE29,
       WE30, WE31;
  wire [31:0] x0, x3, x4, x11, x12, x13, x14, x15, x16, x17, x18, x19, x20, x21, x22, x23, x24, x25, x26,
       x27, x28, x29, x30, x31;

  Register #(.width(32)) x1 (.D(Write_Data), .en(WE1), .clk(clk), .Q(ra));  // open: clr
  Register #(.width(32)) u_x4 (.D(Write_Data), .en(WE4), .clk(clk), .Q(x4));  // open: clr
  Register #(.width(32)) x7 (.D(Write_Data), .en(WE7), .clk(clk), .Q(t2));  // open: clr
  Register #(.width(32)) x10 (.D(Write_Data), .en(WE10), .clk(clk), .Q(a0));  // open: clr
  Register #(.width(32)) u_x13 (.D(Write_Data), .en(WE13), .clk(clk), .Q(x13));  // open: clr
  Register #(.width(32)) u_x16 (.D(Write_Data), .en(WE16), .clk(clk), .Q(x16));  // open: clr
  Register #(.width(32)) u_x19 (.D(Write_Data), .en(WE19), .clk(clk), .Q(x19));  // open: clr
  Register #(.width(32)) u_x22 (.D(Write_Data), .en(WE22), .clk(clk), .Q(x22));  // open: clr
  Register #(.width(32)) u_x25 (.D(Write_Data), .en(WE25), .clk(clk), .Q(x25));  // open: clr
  Register #(.width(32)) u_x28 (.D(Write_Data), .en(WE28), .clk(clk), .Q(x28));  // open: clr
  Register #(.width(32)) u_x31 (.D(Write_Data), .en(WE31), .clk(clk), .Q(x31));  // open: clr
  Register #(.width(32)) x2 (.D(Write_Data), .en(WE2), .clk(clk), .Q(sp));  // open: clr
  Register #(.width(32)) x5 (.D(Write_Data), .en(WE5), .clk(clk), .Q(t0));  // open: clr
  Register #(.width(32)) x8 (.D(Write_Data), .en(WE8), .clk(clk), .Q(s0));  // open: clr
  Register #(.width(32)) u_x11 (.D(Write_Data), .en(WE11), .clk(clk), .Q(x11));  // open: clr
  Register #(.width(32)) u_x14 (.D(Write_Data), .en(WE14), .clk(clk), .Q(x14));  // open: clr
  Register #(.width(32)) u_x17 (.D(Write_Data), .en(WE17), .clk(clk), .Q(x17));  // open: clr
  Register #(.width(32)) u_x20 (.D(Write_Data), .en(WE20), .clk(clk), .Q(x20));  // open: clr
  Register #(.width(32)) u_x23 (.D(Write_Data), .en(WE23), .clk(clk), .Q(x23));  // open: clr
  Register #(.width(32)) u_x26 (.D(Write_Data), .en(WE26), .clk(clk), .Q(x26));  // open: clr
  Register #(.width(32)) u_x29 (.D(Write_Data), .en(WE29), .clk(clk), .Q(x29));  // open: clr
  Register #(.width(32)) u_x0 (.D(Write_Data), .en(WE0), .clk(clk), .Q(x0), .clr(1'b1));
  Register #(.width(32)) u_x3 (.D(Write_Data), .en(WE3), .clk(clk), .Q(x3));  // open: clr
  Register #(.width(32)) x6 (.D(Write_Data), .en(WE6), .clk(clk), .Q(t1));  // open: clr
  Register #(.width(32)) x9 (.D(Write_Data), .en(WE9), .clk(clk), .Q(s1));  // open: clr
  Register #(.width(32)) u_x12 (.D(Write_Data), .en(WE12), .clk(clk), .Q(x12));  // open: clr
  Register #(.width(32)) u_x15 (.D(Write_Data), .en(WE15), .clk(clk), .Q(x15));  // open: clr
  Register #(.width(32)) u_x18 (.D(Write_Data), .en(WE18), .clk(clk), .Q(x18));  // open: clr
  Register #(.width(32)) u_x21 (.D(Write_Data), .en(WE21), .clk(clk), .Q(x21));  // open: clr
  Register #(.width(32)) u_x24 (.D(Write_Data), .en(WE24), .clk(clk), .Q(x24));  // open: clr
  Register #(.width(32)) u_x27 (.D(Write_Data), .en(WE27), .clk(clk), .Q(x27));  // open: clr
  Register #(.width(32)) u_x30 (.D(Write_Data), .en(WE30), .clk(clk), .Q(x30));  // open: clr
  Multiplexer #(.enable("false"), .select(5), .width(32)) multiplexer_1 (
    .in0(x0), .in1(ra), .in2(sp), .in3(x3), .in4(x4), .in5(t0), .in6(t1), .in7(t2), .in8(s0), .in9(s1),
    .in10(a0), .in11(x11), .in12(x12), .in13(x13), .in14(x14), .in15(x15), .in16(x16), .in17(x17),
    .in18(x18), .in19(x19), .in20(x20), .in21(x21), .in22(x22), .in23(x23), .in24(x24), .in25(x25),
    .in26(x26), .in27(x27), .in28(x28), .in29(x29), .in30(x30), .in31(x31), .out(Read_Data_1), .sel(rs1));
  Multiplexer #(.enable("false"), .select(5), .width(32)) multiplexer_2 (
    .in0(x0), .in1(ra), .in2(sp), .in3(x3), .in4(x4), .in5(t0), .in6(t1), .in7(t2), .in8(s0), .in9(s1),
    .in10(a0), .in11(x11), .in12(x12), .in13(x13), .in14(x14), .in15(x15), .in16(x16), .in17(x17),
    .in18(x18), .in19(x19), .in20(x20), .in21(x21), .in22(x22), .in23(x23), .in24(x24), .in25(x25),
    .in26(x26), .in27(x27), .in28(x28), .in29(x29), .in30(x30), .in31(x31), .out(Read_Data_2), .sel(rs2));
  and and_1 (WE0, RegWEn, decoder_1_out0);
  and and_2 (WE1, RegWEn, decoder_1_out1);
  and and_3 (WE2, RegWEn, decoder_1_out2);
  and and_4 (WE3, RegWEn, decoder_1_out3);
  and and_5 (WE4, RegWEn, decoder_1_out4);
  and and_6 (WE5, RegWEn, decoder_1_out5);
  and and_7 (WE6, RegWEn, decoder_1_out6);
  and and_8 (WE7, RegWEn, decoder_1_out7);
  and and_9 (WE8, RegWEn, decoder_1_out8);
  and and_10 (WE9, RegWEn, decoder_1_out9);
  and and_11 (WE10, RegWEn, decoder_1_out10);
  and and_12 (WE11, RegWEn, decoder_1_out11);
  and and_13 (WE12, RegWEn, decoder_1_out12);
  and and_14 (WE13, RegWEn, decoder_1_out13);
  and and_15 (WE14, RegWEn, decoder_1_out14);
  and and_16 (WE15, RegWEn, decoder_1_out15);
  and and_17 (WE16, RegWEn, decoder_1_out16);
  and and_18 (WE17, RegWEn, decoder_1_out17);
  and and_19 (WE18, RegWEn, decoder_1_out18);
  and and_20 (WE19, RegWEn, decoder_1_out19);
  and and_21 (WE20, RegWEn, decoder_1_out20);
  and and_22 (WE21, RegWEn, decoder_1_out21);
  and and_23 (WE22, RegWEn, decoder_1_out22);
  and and_24 (WE23, RegWEn, decoder_1_out23);
  and and_25 (WE24, RegWEn, decoder_1_out24);
  and and_26 (WE25, RegWEn, decoder_1_out25);
  and and_27 (WE26, RegWEn, decoder_1_out26);
  and and_28 (WE27, RegWEn, decoder_1_out27);
  and and_29 (WE28, RegWEn, decoder_1_out28);
  and and_30 (WE29, RegWEn, decoder_1_out29);
  and and_31 (WE30, RegWEn, decoder_1_out30);
  and and_32 (WE31, RegWEn, decoder_1_out31);
  Decoder #(.enable("false"), .select(5)) decoder_1 (
    .out0(decoder_1_out0), .out1(decoder_1_out1), .out2(decoder_1_out2), .out3(decoder_1_out3),
    .out4(decoder_1_out4), .out5(decoder_1_out5), .out6(decoder_1_out6), .out7(decoder_1_out7),
    .out8(decoder_1_out8), .out9(decoder_1_out9), .out10(decoder_1_out10), .out11(decoder_1_out11),
    .out12(decoder_1_out12), .out13(decoder_1_out13), .out14(decoder_1_out14), .out15(decoder_1_out15),
    .out16(decoder_1_out16), .out17(decoder_1_out17), .out18(decoder_1_out18), .out19(decoder_1_out19),
    .out20(decoder_1_out20), .out21(decoder_1_out21), .out22(decoder_1_out22), .out23(decoder_1_out23),
    .out24(decoder_1_out24), .out25(decoder_1_out25), .out26(decoder_1_out26), .out27(decoder_1_out27),
    .out28(decoder_1_out28), .out29(decoder_1_out29), .out30(decoder_1_out30), .out31(decoder_1_out31),
    .sel(rd));

  // Other names for the same wires on the sheet: read_data1[31:0] = Read_Data_1; read_data2[31:0] = Read_Data_2;
  //   read_reg1[4:0] = rs1; read_reg2[4:0] = rs2; write_en = RegWEn; write_reg[4:0] = rd; x1[31:0] = ra;
  //   x2[31:0] = sp; x5[31:0] = t0; x6[31:0] = t1; x7[31:0] = t2; x8[31:0] = s0; x9[31:0] = s1; x10[31:0] = a0

  // Notes on the sheet:
  //   INPUTS to your circuit
  //   DON'T CHANGE THE LOCATIONS OF THE INPUTS AND OUTPUTS!
  //   These are DEBUG/TEST outputs from your circuit.
  //   OUTPUTS from your circuit
endmodule
